# Fritzing sketch Arduino_max485_shield (saved by Fritzing 0.9.4)
circuit board: 7.00001cm x 7.00001cm
breadboards: 1

parts:
  rfid_reader = RFID-RC522-v2
  LedR = LED - 5mm [color="Red (633nm)" package="5 mm [THT]"]
  LedV = LED - 5mm [color="Green (560nm)" package="5 mm [THT]"]
  LedB = LED - 5mm [color="Blue (505nm)" package="5 mm [THT]"]
  R2 = Resistor [tolerance=±5% resistance=220 package=THT]
  R3 = Resistor [tolerance=±5% resistance=220 package=THT]
  R4 = Resistor [tolerance=±5% resistance=220 package=THT]
  Arduino = Arduino Pro Mini v13
  Term = Resistor [tolerance=±5% resistance=120 package=THT]
  485 = Module RS485 [package=board]
  Relay_output = screw terminal, 3 pins
  Phone_power = screw terminal, 2 pins

nets:
  N1: rfid_reader.SDA, Arduino.D10_PWM/SS
  N2: rfid_reader.SCK, Arduino.D13/SCK
  N3: rfid_reader.MOSI, Arduino.D11_PWM/MOSI
  N4: rfid_reader.MISO, Arduino.D12/MISO
  GND: rfid_reader.GND, LedR.cathode, LedV.cathode, LedB.cathode, Arduino.GND, 485.GND, Relay_output.pin3, Phone_power.pin1
  N5: rfid_reader.RST, Arduino.D7
  3.3V: rfid_reader.3.3V, Arduino.VCC
  N6: LedR.anode, R3.Pin_0
  N7: LedV.anode, R2.Pin_0
  N8: LedB.anode, R4.Pin_0
  N9: R2.Pin_1, Arduino.D5_PWM
  N10: R3.Pin_1, Arduino.D4
  N11: R4.Pin_1, Arduino.D6_PWM
  N12: Arduino.A5, Arduino.RESET
  N13: Arduino.RAW, 485.VCC, Relay_output.pin2, Phone_power.pin2
  N14: Arduino.D9_PWM, 485.RE, 485.DE
  N15: Arduino.D8, Relay_output.pin1
  N16: Arduino.D1/RX, 485.RO
  N17: Arduino.D0/TX, 485.DI
  N18: Term.Pin_0, 485.A
  N19: Term.Pin_1, 485.B

notes:
  GND
  +5V

custom parts:
  RFID-RC522-v2: A simple China made RFID-RC522 Reader; do check the pin labels, as this is a MFRC522 based clone.
  Arduino Pro Mini v13: It's blue! It's thin! It's the Arduino Pro Mini! SparkFun's minimal design approach to Arduino. This is a 5V Arduino running the 16MHz bootloader. Arduino Pro Mini does not come with connectors populated so that you can solder in any connector or wire with any orientation you need. We recommend first time Arduino users start with the Uno R3. It's a great board that will get you up and running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
  Module RS485: RS-485 transceiver V1
