# Fritzing sketch RPi_max485_shield (saved by Fritzing 0.9.4)
circuit board: 6.6cm x 5.02475cm
breadboards: 1

parts:
  Raspberry_Pi_1 = Raspberry Pi 3 [part_number=RPI-3-V1.2]
  IN_5-30V = Screw terminal - 2 pins [package=THT]
  X1 = USB Connectors [package=s4b-ph]
  Term = Resistor [tolerance=±5% resistance=120 package=THT]
  OUT_5v_(periph) = screw terminal, 2 pins
  M4 = RioRand LM2596
  485 = Module RS485 [package=board]

nets:
  GND: Raspberry_Pi_1.GND, X1.GND, OUT_5v_(periph).pin1, M4.Pin_1, 485.GND
  N1: Raspberry_Pi_1.GIPO23, 485.RE, 485.DE
  N2: Raspberry_Pi_1.GIPO15, 485.RO
  N3: Raspberry_Pi_1.GIPO14, 485.DI
  N4: IN_5-30V.pin1, M4.Pin_3
  N5: IN_5-30V.pin2, M4.Pin_4
  N6: X1.VBUS, OUT_5v_(periph).pin2, M4.Pin_2, 485.VCC
  N7: Term.Pin_0, 485.B
  N8: Term.Pin_1, 485.A

notes:
  LM2596
  - - >
  In+
  In-
  +5V
  GND

custom parts:
  RioRand LM2596: Step-down DC-DC Converter (modified to correct all views by Peter Van Epp january 2018) Corrected the pins so the part works in all views. Changed the sizes in bb and pcb to match the data sheet. PCB view had a small outline (possibly only for wires), changed it to pads in the same places as the module and added holes in the PCB silkscreen layer where the mounting holes on the module are (you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
  Module RS485: RS-485 transceiver V1
